# Fritzing sketch diagrama (saved by Fritzing 1.0.4)
breadboards: 1

parts:
  Mod1 = Amica NodeMCU DEVKIT 1.0
  HC-SR04_Sensor_1 = HC-SR04 Ultrasonic Distance Sensor
  M1 = 1 chan 5v relay module
  Mod2 = Passive Buzzer
  R1 = Resistor [tolerance=±5% power=0.25W resistance=1k package=THT]
  R2 = Resistor [tolerance=±5% power=0.25W resistance=15k package=THT]

nets:
  N1: Mod1.pin1, Mod1.pin_10, Mod1.pin_26
  N2: Mod1.pin2, Mod1.pin_9, Mod1.pin_18, Mod1.pin_25, Mod1.pin_29, HC-SR04_Sensor_1.GND, M1.pin_1, Mod2.NC, R2.Pin_1
  N3: Mod1.pin5, Mod2.S
  N4: Mod1.pin6, R1.Pin_1, R2.Pin_0
  N5: Mod1.pin8, M1.pin_3
  N6: Mod1.pin_14, HC-SR04_Sensor_1.TRIG
  N7: HC-SR04_Sensor_1.ECHO, R1.Pin_0
  N8: M1.pin_2, Mod2.-

custom parts:
  1 chan 5v relay module: 1 Channel 5V Relay Module Board Shield with Optocoupler Support High and Low Level Trigger for Arduino.
